# Fritzing sketch simon (saved by Fritzing 0.9.3b)
breadboards: 1

parts:
  Componente1 = Arduino Nano (Rev3.0)
  SP1 = SPEAKER [package=pcb_mount_speaker]
  LED1 = LED - 5mm [color="Red (633nm)" package="5 mm [THT]"]
  part = Resistor [tolerance=±5% resistance=220 package=THT]
  part_2 = Resistor [tolerance=±5% resistance=220 package=THT]
  LED2 = LED - 5mm [color="Red (633nm)" package="5 mm [THT]"]
  part_3 = Resistor [tolerance=±5% resistance=220 package=THT]
  LED3 = LED - 5mm [color="Red (633nm)" package="5 mm [THT]"]
  R1 = Resistor [tolerance=±5% resistance=220 package=THT]
  LED4 = LED - 5mm [color="Red (633nm)" package="5 mm [THT]"]
  part_4 = Resistor [tolerance=±5% resistance=100k package=THT]
  part_5 = Resistor [tolerance=±5% resistance=100k package=THT]
  S1 = Pushbutton [package="[THT]"]
  S2 = Pushbutton [package="[THT]"]
  S3 = Pushbutton [package="[THT]"]
  S4 = Pushbutton [package="[THT]"]
  part_6 = Resistor [tolerance=±5% resistance=3.3k package=THT]
  part_7 = Resistor [tolerance=±5% resistance=47k package=THT]

nets:
  N1: Componente1.GND, SP1.-, LED1.cathode, LED2.cathode, LED3.cathode, LED4.cathode, part_4.Pin_1, part_5.Pin_1, S1.Pin_1, S1.Pin_2, S2.Pin_1, S2.Pin_2, S3.Pin_1, S3.Pin_2, S4.Pin_1, S4.Pin_2
  N2: Componente1.D3, SP1.+
  N3: Componente1.D4, part.Pin_0
  N4: Componente1.D5, part_2.Pin_0
  N5: Componente1.D6, part_3.Pin_0
  N6: Componente1.D7, R1.Pin_0
  N7: Componente1.5V, part_6.Pin_0, part_7.Pin_1
  N8: Componente1.A1, part_5.Pin_0
  N9: Componente1.A0, part_4.Pin_0
  N10: LED1.anode, part.Pin_1
  N11: part_2.Pin_1, LED2.anode
  N12: S1.Pin_3, S1.Pin_4, S3.Pin_3, S3.Pin_4, part_7.Pin_0
  N13: S2.Pin_3, S2.Pin_4, S4.Pin_3, S4.Pin_4
